# Fritzing sketch lm35_schema (saved by Fritzing 0.9.3b)
breadboards: 1

parts:
  T1 = LM35 Temperature Sensor [package="TO92 [THT]"]
  Launchpad1 = TI Launchpad TM4C123GXL
  V1 = DC Power [voltage=5]

nets:
  N1: T1.+Vs, V1.V+
  N2: T1.Vout, Launchpad1.PD2
  N3: T1.GND, V1.V-
